# Fritzing sketch MagicDrinksDispenser (saved by Fritzing 0.9.3b)
breadboards: 1

parts:
  Q1 = TIP120 Hi-Current Darlington Transistor
  Q2 = Basic FET N-Channel [package="TO220 [THT]"]
  Part1 = Arduino Nano (Rev3.0)
  J1 = Screw terminal - 2 pins [package=THT]
  J2 = Screw terminal - 2 pins [package=THT]
  J3 = Screw terminal - 2 pins [package=THT]
  D1 = Rectifier Diode [part_number=1N4001 package="300 mil [THT]"]
  R1 = Resistor [tolerance=±5% resistance=1k package=THT]
  Power_plug1 = Power plug
  R2 = Resistor [tolerance=±5% resistance=4.7k package=THT]
  J4 = female pin header, 5 pins [form="♀ (female)"]
  M1 = DC Motor
  D2 = Rectifier Diode [part_number=1N4001 package="300 mil [THT]"]
  R3 = Resistor [tolerance=±5% resistance=10k package=THT]
  J5 = Screw terminal - 2 pins [package=THT]

nets:
  N1: Q1.BASE, R2.Pin_1
  N2: Q1.COLLECTOR, J3.pin1, D1.anode, M1.pin_2
  GND: Q1.EMITTER, Q2.source, Part1.GND, J1.pin1, Power_plug1.GND, R3.Pin_0
  N3: Q2.gate, R1.Pin_1
  N4: Q2.drain, J2.pin1
  N5: Part1.D2, J4.pin5
  N6: Part1.D3, J4.pin4
  N7: Part1.D4, J4.pin3
  N8: Part1.D5, J4.pin2
  N9: Part1.D6, J4.pin1
  N10: Part1.D9, R2.Pin_0
  N11: Part1.D10, R1.Pin_0, R3.Pin_1
  VIN: Part1.VIN, J1.pin2, J2.pin2, J3.pin2, D1.cathode, Power_plug1.VCC, M1.pin_1, D2.cathode
  N12: Part1.5V, D2.anode
  N13: Part1.A1, J5.pin2
  N14: Part1.A0, J5.pin1
